# Fritzing sketch TWO-BUTTONS-LED (saved by Fritzing 0.9.3b)
circuit board: 8.46667cm x 5.64444cm
breadboards: 1

parts:
  元件1 = Arduino Uno (Rev3)
  S1 = Pushbutton [package="[THT]"]
  LED1 = smd LED [color="Red (633nm)" package="0805 [SMD]"]
  S2 = Pushbutton [package="[THT]"]

nets:
  N1: 元件1.D13/SCK, LED1.anode
  N2: 元件1.GND, S1.Pin_3, S1.Pin_4, S2.Pin_3, S2.Pin_4
  N3: 元件1.D1/TX, 元件1.D2, S2.Pin_1, S2.Pin_2
  N4: 元件1.D3_PWM, S1.Pin_1, S1.Pin_2
  N5: 元件1.5V, LED1.cathode

notes:
  TWO BUTTONS AND PIN13 LED
